# Fritzing sketch Example (saved by Fritzing 1.0.1rc)
breadboards: 1

parts:
  Part1 = Arduino BT
  U1 = ENCODER-QUADRATURE [package=encoder-16mm-quad]

nets:
  N1: Part1.D2, U1.C
  N2: Part1.PWM_D3, U1.A
  N3: Part1.GND, U1.B
